# Fritzing sketch workshop (saved by Fritzing 0.9.9b)
breadboards: 1

parts:
  Mod1 = Raspberry Pi Pico W
  LED = smd LED [color="Red (633nm)" package="0603 [SMD]"]
  R = Resistor [tolerance=±5% power=0.25 resistance=220 package=THT]
  Mod2 = Raspberry Pi Pico W
  U1 = POT [package=pot_mammoth]
  S = Round Pushbutton

nets:
  N1: Mod1.pin_1, Mod2.pin_7
  N2: Mod1.pin_2, Mod2.pin_6
  N3: Mod1.pin_3, Mod1.pin_8, Mod1.pin_13, Mod1.pin_18, Mod1.pin_23, Mod1.pin_28, Mod1.pin_33, Mod1.pin_38, Mod1.pin_42, LED.cathode, Mod2.pin_3, Mod2.pin_42, U1.E
  N4: Mod1.pin_19, S.leg1
  N5: Mod1.pin_20, R.Pin_1
  N6: Mod1.pin_31, U1.A
  N7: Mod1.pin_39, Mod2.pin_39, U1.S, S.leg0
  N8: Mod1.pin_41, Mod2.pin_4
  N9: Mod1.pin_43, Mod2.pin_5
  N10: LED.anode, R.Pin_0

custom parts:
  Raspberry Pi Pico W: Raspberry Pi Pico W. Based around the RP2040 microcontroller the Pico W is a low cost microcontroller device bringing Raspberry Pi quality, cost, and easy of use to the microcontroller space. The areas marked KEEPOUT in pcb silkscreen should not have traces running through them to avoid shorts on a soldered in module!
